// Logisim project ex1.circ as structural Verilog: 1 circuit, main circuit Split
module Split (
  input  [7:0] IN1,
  output OUT1,
  output OUT2,
  output [8:0] OUT3,
  output [8:0] OUT4
);

  wire [3:0] bitadder_1_out, bitadder_2_out;
  wire [7:0] not_2_out;
  wire [8:0] adder_1_out, bit_extender_1_out, not_3_out;

  not not_1 (OUT3[8], OUT1);
  ExactlyOne xor_1 (
    .out(OUT1), .in0(IN1[0]), .in1(IN1[1]), .in2(IN1[2]), .in3(IN1[3]), .in4(IN1[4]), .in5(IN1[5]),
    .in6(IN1[6]), .in7(IN1[7]));
  assign not_2_out = ~IN1;  // NOT_Gate not_2, 8 bits wide
  assign bit_extender_1_out = {{8{OUT2}}, OUT2};  // Bit_Extender bit_extender_1
  assign not_3_out = ~{OUT2, IN1};  // NOT_Gate not_3, 9 bits wide
  BitAdder bitadder_1 (.in0(IN1), .out(bitadder_1_out));
  BitAdder bitadder_2 (.in0(not_2_out), .out(bitadder_2_out));
  Adder #(.width(9)) adder_1 (.a(bit_extender_1_out), .b(not_3_out), .out(adder_1_out));  // open: cin, cout
  Comparator #(.width(4)) comparator_1 (.a(bitadder_1_out), .b(bitadder_2_out), .gt(OUT2));  // open: eq, lt
  Multiplexer #(.width(9), .enable("false")) multiplexer_1 (
    .in0({OUT2, IN1}), .in1(adder_1_out), .out(OUT4), .sel(OUT2));

  assign OUT3[7:0] = IN1;

  // Other names for the same wires on the sheet: IN1_0 = IN1[0]; IN1_1 = IN1[1]; IN1_2 = IN1[2]; IN1_3 = IN1[3];
  //   IN1_4 = IN1[4]; IN1_5 = IN1[5]; IN1_6 = IN1[6]; IN1_7 = IN1[7]

  // Notes on the sheet:
  //   PUT CIRCUITRY HERE
endmodule
