// Logisim project cpu.circ as structural Verilog: 7 circuits, main circuit main
module main (
  input  [31:0] INSTRUCTION,
  input  CLOCK,
  output [31:0] FETCH_ADDRESS,
  output [31:0] ra,
  output [31:0] sp,
  output [31:0] t0,
  output [31:0] t1,
  output [31:0] t2,
  output [31:0] s0,
  output [31:0] s1,
  output [31:0] a0
);

  wire BrEq, BrLT, BrUn, lui, mem_rw, op_src, pc_sel, pc_src, reg_we;
  wire [1:0] d_src;
  wire [2:0] imm_sel, load_type;
  wire [3:0] alu_ctrl;
  wire [4:0] dec_1_rd, dec_1_rs1, dec_1_rs2;
  wire [31:0] adder_1_out, adder_2_out, alu_1_result, data_mem_1_result, dec_1_imm, imm_gen_1_imme,
       main_1_read_data_1, main_1_read_data_2, multiplexer_1_out, multiplexer_2_out, multiplexer_3_out,
       multiplexer_4_out, multiplexer_5_out, multiplexer_6_out, pc_1_programcounter, register_1_q,
       register_2_q;

  Adder #(.width(32)) adder_1 (.a(pc_1_programcounter), .b(32'h4), .out(adder_1_out));  // open: cin, cout
  Multiplexer #(.width(32), .enable("false")) multiplexer_1 (
    .in0(INSTRUCTION), .in1(32'h13), .out(multiplexer_1_out), .sel(pc_sel));
  Multiplexer #(.width(32), .enable("false")) multiplexer_2 (
    .in0(adder_1_out), .in1(alu_1_result), .out(multiplexer_2_out), .sel(pc_sel));
  Register #(.width(32)) register_1 (.D(multiplexer_1_out), .en(1'b1), .clk(CLOCK), .Q(register_1_q));  // open: clr
  PC pc_1 (.value(multiplexer_2_out), .clk(CLOCK), .ProgramCounter(pc_1_programcounter));
  Dec dec_1 (.inst(register_1_q), .rd(dec_1_rd), .rs1(dec_1_rs1), .rs2(dec_1_rs2), .imm(dec_1_imm));
  Ctrl ctrl_1 (
    .inst(register_1_q), .BrEq(BrEq), .BrLt(BrLT), .pc_sel(pc_sel), .reg_we(reg_we), .imm_sel(imm_sel),
    .BrUn(BrUn), .op_src(op_src), .pc_src(pc_src), .alu_ctrl(alu_ctrl), .mem_rw(mem_rw), .d_src(d_src),
    .load_type(load_type), .lui(lui));
  Shifter #(.width(32), .shift("lr")) shifter_1 (.in(pc_1_programcounter), .\dist (5'b00010), .out(FETCH_ADDRESS));
  Imm_Gen imm_gen_1 (.imm(dec_1_imm), .imm_sel(imm_sel), .IMME(imm_gen_1_imme));
  Register #(.width(32)) register_2 (.D(pc_1_programcounter), .en(1'b1), .clk(CLOCK), .Q(register_2_q));  // open: clr
  regfile_main main_1 (
    .rs2(dec_1_rs2), .rd(dec_1_rd), .Read_Data_1(main_1_read_data_1), .Read_Data_2(main_1_read_data_2),
    .ra(ra), .sp(sp), .t0(t0), .t1(t1), .t2(t2), .s0(s0), .s1(s1), .a0(a0), .rs1(dec_1_rs1),
    .Write_Data(multiplexer_6_out), .RegWEn(reg_we), .clk(CLOCK));
  Adder #(.width(32)) adder_2 (.a(register_2_q), .b(32'h4), .out(adder_2_out));  // open: cin, cout
  Multiplexer #(.width(32), .enable("false")) multiplexer_3 (
    .in0(main_1_read_data_1), .in1(register_2_q), .out(multiplexer_3_out), .sel(pc_src));
  CompLogic complogic_1 (.x_rs1(main_1_read_data_1), .x_rs2(main_1_read_data_2), .BrUn(BrUn), .BrLt(BrLT), .BrEq(BrEq));
  Multiplexer #(.width(32), .enable("false")) multiplexer_4 (
    .in0(main_1_read_data_2), .in1(imm_gen_1_imme), .out(multiplexer_4_out), .sel(op_src));
  Multiplexer #(.width(32), .enable("false")) multiplexer_5 (
    .in0(multiplexer_3_out), .in1({32{1'b0}}), .out(multiplexer_5_out), .sel(lui));
  alu alu_1 (.A(multiplexer_5_out), .B(multiplexer_4_out), .ALUSel(alu_ctrl), .Result(alu_1_result));
  Data_Mem data_mem_1 (
    .alu_res(alu_1_result), .mem_rw(mem_rw), .clk(CLOCK), .x_rs2(main_1_read_data_2), .load_type(load_type),
    .result(data_mem_1_result));
  Multiplexer #(.select(2), .width(32), .enable("false")) multiplexer_6 (
    .in0(data_mem_1_result), .in1(alu_1_result), .in2(adder_2_out), .out(multiplexer_6_out), .sel(d_src));  // open: in3

  // Other names for the same wires on the sheet: clk = CLOCK; fetch_addr[31:0] = FETCH_ADDRESS

  // Notes on the sheet:
  //   Output
  //   Inputs/Outputs from run.circ. DO NOT MOVE THESE.
  //   Inputs
  //   Inputs/Outputs from run.circ. DO NOT MOVE THESE.
endmodule

module PC (
  input  [31:0] value,
  input  clk,
  output [31:0] ProgramCounter
);

  Register #(.width(32)) register_1 (.D(value), .en(1'b1), .clk(clk), .Q(ProgramCounter));  // open: clr
endmodule

module Dec (
  input  [31:0] inst,
  output [4:0] rd,
  output [4:0] rs1,
  output [4:0] rs2,
  output [31:0] imm
);

  wire [31:0] bit_extender_1_out;

  assign bit_extender_1_out = {{7{1'b0}}, inst[31:7]};  // Bit_Extender bit_extender_1
  Shifter #(.width(32)) shifter_1 (.in(bit_extender_1_out), .\dist (5'b00111), .out(imm));

  assign rd = inst[11:7];
  assign rs1 = inst[19:15];
  assign rs2 = inst[24:20];
endmodule

module Ctrl (
  input  [31:0] inst,
  input  BrEq,
  input  BrLt,
  output pc_sel,
  output reg_we,
  output [2:0] imm_sel,
  output BrUn,
  output op_src,
  output pc_src,
  output [3:0] alu_ctrl,
  output mem_rw,
  output [1:0] d_src,
  output [2:0] load_type,
  output lui
);

  wire a_n_d, add, add_type, addi, alu, andi, beq, beq_type, bgeu, bgeu_type, blt, blt_type, bltu, bltu_type,
       bne, bne_type, comparator_1_eq, comparator_2_eq, comparator_3_eq, comparator_4_eq, comparator_5_eq,
       comparator_6_eq, comparator_7_eq, comparator_8_eq, comparator_9_eq, comparator_10_eq,
       comparator_11_eq, comparator_12_eq, comparator_13_eq, comparator_14_eq, comparator_15_eq,
       comparator_16_eq, comparator_17_eq, comparator_18_eq, comparator_19_eq, comparator_20_eq,
       comparator_21_eq, comparator_22_eq, comparator_23_eq, comparator_24_eq, comparator_25_eq,
       comparator_26_eq, comparator_27_eq, comparator_28_eq, comparator_38_eq, comparator_39_eq,
       comparator_40_eq, comparator_41_eq, comparator_42_eq, comparator_43_eq, comparator_44_eq,
       comparator_45_eq, comparator_46_eq, comparator_47_eq, comparator_48_eq, comparator_49_eq,
       comparator_50_eq, comparator_51_eq, comparator_52_eq, comparator_53_eq, comparator_54_eq,
       comparator_55_eq, comparator_56_eq, comparator_57_eq, div, divu, I, Itype, Itype_jalr, Itype_load, lb,
       lbu, lh, lhu, lw, mul, mulh, mulhu, not_2_out, not_3_out, o_r, or_11_out, or_12_out, or_type, ori,
       remu, Rtype, s_l_l, s_r_a, s_r_l, SBtype, sll_type, slli, slti, srl_type, srli, Stype, sub, UJtype,
       Utype, Utype_auipc, x_o_r, xor_type, xori;
  wire [1:0] multiplexer_8_out;
  wire [2:0] multiplexer_4_out, multiplexer_6_out, multiplexer_10_out, multiplexer_18_out,
       multiplexer_20_out, multiplexer_22_out;
  wire [3:0] multiplexer_1_out, multiplexer_2_out, multiplexer_3_out, multiplexer_5_out, multiplexer_7_out,
       multiplexer_9_out, multiplexer_12_out, multiplexer_13_out, multiplexer_15_out, multiplexer_16_out,
       multiplexer_17_out, multiplexer_19_out, multiplexer_21_out;

  Comparator #(.width(3)) comparator_1 (.a(inst[14:12]), .b(3'b000), .eq(comparator_1_eq));  // open: gt, lt
  Comparator #(.width(7)) comparator_2 (.a(inst[31:25]), .b({7{1'b0}}), .eq(comparator_2_eq));  // open: gt, lt
  Comparator #(.width(3)) comparator_3 (.a(inst[14:12]), .b(3'b000), .eq(comparator_3_eq));  // open: gt, lt
  Comparator #(.width(7)) comparator_4 (.a(inst[31:25]), .b(7'b0000001), .eq(comparator_4_eq));  // open: gt, lt
  Comparator #(.width(3)) comparator_5 (.a(inst[14:12]), .b(3'b000), .eq(comparator_5_eq));  // open: gt, lt
  Comparator #(.width(7)) comparator_6 (.a(inst[31:25]), .b(7'b0100000), .eq(comparator_6_eq));  // open: gt, lt
  Comparator #(.width(3)) comparator_7 (.a(inst[14:12]), .b(3'b001), .eq(comparator_7_eq));  // open: gt, lt
  Comparator #(.width(7)) comparator_8 (.a(inst[31:25]), .b({7{1'b0}}), .eq(comparator_8_eq));  // open: gt, lt
  Comparator #(.width(3)) comparator_9 (.a(inst[14:12]), .b(3'b001), .eq(comparator_9_eq));  // open: gt, lt
  Comparator #(.width(7)) comparator_10 (.a(inst[31:25]), .b(7'b0000001), .eq(comparator_10_eq));  // open: gt, lt
  Comparator #(.width(3)) comparator_11 (.a(inst[14:12]), .b(3'b011), .eq(comparator_11_eq));  // open: gt, lt
  Comparator #(.width(7)) comparator_12 (.a(inst[31:25]), .b(7'b0000001), .eq(comparator_12_eq));  // open: gt, lt
  Comparator #(.width(3)) comparator_13 (.a(inst[14:12]), .b(3'b100), .eq(comparator_13_eq));  // open: gt, lt
  Comparator #(.width(7)) comparator_14 (.a(inst[31:25]), .b({7{1'b0}}), .eq(comparator_14_eq));  // open: gt, lt
  Comparator #(.width(3)) comparator_15 (.a(inst[14:12]), .b(3'b100), .eq(comparator_15_eq));  // open: gt, lt
  Comparator #(.width(7)) comparator_16 (.a(inst[31:25]), .b(7'b0000001), .eq(comparator_16_eq));  // open: gt, lt
  Comparator #(.width(3)) comparator_17 (.a(inst[14:12]), .b(3'b101), .eq(comparator_17_eq));  // open: gt, lt
  Comparator #(.width(7)) comparator_18 (.a(inst[31:25]), .b(7'b0000001), .eq(comparator_18_eq));  // open: gt, lt
  Comparator #(.width(3)) comparator_19 (.a(inst[14:12]), .b(3'b101), .eq(comparator_19_eq));  // open: gt, lt
  Comparator #(.width(7)) comparator_20 (.a(inst[31:25]), .b({7{1'b0}}), .eq(comparator_20_eq));  // open: gt, lt
  Comparator #(.width(3)) comparator_21 (.a(inst[14:12]), .b(3'b110), .eq(comparator_21_eq));  // open: gt, lt
  Comparator #(.width(7)) comparator_22 (.a(inst[31:25]), .b({7{1'b0}}), .eq(comparator_22_eq));  // open: gt, lt
  Comparator #(.width(3)) comparator_23 (.a(inst[14:12]), .b(3'b111), .eq(comparator_23_eq));  // open: gt, lt
  Comparator #(.width(7)) comparator_24 (.a(inst[31:25]), .b(7'b0000001), .eq(comparator_24_eq));  // open: gt, lt
  Comparator #(.width(3)) comparator_25 (.a(inst[14:12]), .b(3'b111), .eq(comparator_25_eq));  // open: gt, lt
  Comparator #(.width(7)) comparator_26 (.a(inst[31:25]), .b({7{1'b0}}), .eq(comparator_26_eq));  // open: gt, lt
  Comparator #(.width(3)) comparator_27 (.a(inst[14:12]), .b(3'b101), .eq(comparator_27_eq));  // open: gt, lt
  Comparator #(.width(7)) comparator_28 (.a(inst[31:25]), .b(7'b0100000), .eq(comparator_28_eq));  // open: gt, lt
  and and_1 (add, comparator_1_eq, Rtype, comparator_2_eq);
  and and_2 (mul, comparator_3_eq, Rtype, comparator_4_eq);
  and and_3 (sub, comparator_5_eq, Rtype, comparator_6_eq);
  and and_4 (s_l_l, comparator_7_eq, Rtype, comparator_8_eq);
  and and_5 (mulh, comparator_9_eq, Rtype, comparator_10_eq);
  and and_6 (mulhu, comparator_11_eq, Rtype, comparator_12_eq);
  and and_7 (x_o_r, comparator_13_eq, Rtype, comparator_14_eq);
  and and_8 (div, comparator_15_eq, Rtype, comparator_16_eq);
  and and_9 (divu, comparator_17_eq, Rtype, comparator_18_eq);
  and and_10 (s_r_l, comparator_19_eq, Rtype, comparator_20_eq);
  and and_11 (o_r, comparator_21_eq, Rtype, comparator_22_eq);
  and and_12 (remu, comparator_23_eq, Rtype, comparator_24_eq);
  and and_13 (a_n_d, comparator_25_eq, Rtype, comparator_26_eq);
  and and_14 (s_r_a, comparator_27_eq, Rtype, comparator_28_eq);
  Comparator #(.width(7)) comparator_29 (.a(inst[6:0]), .b(7'b0110011), .eq(Rtype));  // open: gt, lt
  Comparator #(.width(7)) comparator_30 (.a(inst[6:0]), .b(7'b0000011), .eq(Itype_load));  // open: gt, lt
  Comparator #(.width(7)) comparator_31 (.a(inst[6:0]), .b(7'b0010011), .eq(Itype));  // open: gt, lt
  Comparator #(.width(7)) comparator_32 (.a(inst[6:0]), .b(7'b0100011), .eq(Stype));  // open: gt, lt
  Comparator #(.width(7)) comparator_33 (.a(inst[6:0]), .b(7'b1100011), .eq(SBtype));  // open: gt, lt
  Comparator #(.width(7)) comparator_34 (.a(inst[6:0]), .b(7'b0010111), .eq(Utype_auipc));  // open: gt, lt
  Comparator #(.width(7)) comparator_35 (.a(inst[6:0]), .b(7'b0110111), .eq(lui));  // open: gt, lt
  Comparator #(.width(7)) comparator_36 (.a(inst[6:0]), .b(7'b1101111), .eq(UJtype));  // open: gt, lt
  Comparator #(.width(7)) comparator_37 (.a(inst[6:0]), .b(7'b1100111), .eq(Itype_jalr));  // open: gt, lt
  nor nor_1 (reg_we, beq, blt, bltu, bne, bgeu, mem_rw);
  or or_1 (pc_sel, beq_type, blt_type, bltu_type, UJtype, bne_type, bgeu_type, Itype_jalr);
  Comparator #(.width(3)) comparator_38 (.a(inst[14:12]), .b(3'b000), .eq(comparator_38_eq));  // open: gt, lt
  Comparator #(.width(3)) comparator_39 (.a(inst[14:12]), .b(3'b001), .eq(comparator_39_eq));  // open: gt, lt
  Comparator #(.width(3)) comparator_40 (.a(inst[14:12]), .b(3'b010), .eq(comparator_40_eq));  // open: gt, lt
  Comparator #(.width(3)) comparator_41 (.a(inst[14:12]), .b(3'b100), .eq(comparator_41_eq));  // open: gt, lt
  Comparator #(.width(3)) comparator_42 (.a(inst[14:12]), .b(3'b101), .eq(comparator_42_eq));  // open: gt, lt
  Comparator #(.width(3)) comparator_43 (.a(inst[14:12]), .b(3'b010), .eq(comparator_43_eq));  // open: gt, lt
  or or_2 (add_type, add, addi, lui, Utype_auipc, SBtype, UJtype, Itype_jalr);
  and and_15 (lb, comparator_38_eq, Itype_load);
  and and_16 (lh, comparator_39_eq, Itype_load);
  and and_17 (lw, comparator_40_eq, Itype_load);
  and and_18 (lbu, comparator_41_eq, Itype_load);
  and and_19 (lhu, comparator_42_eq, Itype_load);
  and and_20 (mem_rw, comparator_43_eq, Stype);
  or or_3 (or_type, o_r, ori);
  or or_4 (xor_type, x_o_r, xori);
  or or_5 (srl_type, s_r_l, srli);
  or or_6 (sll_type, s_l_l, slli);
  or or_7 (pc_src, beq, bne, blt, bltu, bgeu, UJtype, Utype_auipc);
  not not_1 (op_src, Rtype);
  or or_8 (alu, Rtype, Itype, Utype_auipc, lui);
  Comparator #(.width(3)) comparator_44 (.a(inst[14:12]), .b(3'b000), .eq(comparator_44_eq));  // open: gt, lt
  Comparator #(.width(3)) comparator_45 (.a(inst[14:12]), .b(3'b001), .eq(comparator_45_eq));  // open: gt, lt
  Comparator #(.width(7)) comparator_46 (.a(inst[31:25]), .b({7{1'b0}}), .eq(comparator_46_eq));  // open: gt, lt
  Comparator #(.width(3)) comparator_47 (.a(inst[14:12]), .b(3'b010), .eq(comparator_47_eq));  // open: gt, lt
  Comparator #(.width(3)) comparator_48 (.a(inst[14:12]), .b(3'b100), .eq(comparator_48_eq));  // open: gt, lt
  Comparator #(.width(3)) comparator_49 (.a(inst[14:12]), .b(3'b101), .eq(comparator_49_eq));  // open: gt, lt
  Comparator #(.width(7)) comparator_50 (.a(inst[31:25]), .b({7{1'b0}}), .eq(comparator_50_eq));  // open: gt, lt
  Comparator #(.width(3)) comparator_51 (.a(inst[14:12]), .b(3'b110), .eq(comparator_51_eq));  // open: gt, lt
  Comparator #(.width(3)) comparator_52 (.a(inst[14:12]), .b(3'b111), .eq(comparator_52_eq));  // open: gt, lt
  Multiplexer #(.width(4), .enable("false")) multiplexer_1 (
    .in0(4'b0000), .in1(4'b0001), .out(multiplexer_1_out), .sel(or_type));
  or or_9 (I, Itype_load, Itype, Itype_jalr);
  or or_10 (Utype, lui, Utype_auipc);
  and and_21 (addi, comparator_44_eq, Itype);
  and and_22 (slli, comparator_45_eq, Itype, comparator_46_eq);
  and and_23 (slti, comparator_47_eq, Itype);
  and and_24 (xori, comparator_48_eq, Itype);
  and and_25 (srli, comparator_49_eq, Itype, comparator_50_eq);
  and and_26 (ori, comparator_51_eq, Itype);
  and and_27 (andi, comparator_52_eq, Itype);
  Multiplexer #(.width(4), .enable("false")) multiplexer_2 (
    .in0(multiplexer_1_out), .in1(4'b0010), .out(multiplexer_2_out), .sel(xor_type));
  Multiplexer #(.width(4), .enable("false")) multiplexer_3 (
    .in0(multiplexer_2_out), .in1(4'b0011), .out(multiplexer_3_out), .sel(add_type));
  Multiplexer #(.width(3), .enable("false")) multiplexer_4 (
    .in0(3'b000), .in1(3'b001), .out(multiplexer_4_out), .sel(Stype));
  Multiplexer #(.width(4), .enable("false")) multiplexer_5 (
    .in0(multiplexer_3_out), .in1(4'b0100), .out(multiplexer_5_out), .sel(sub));
  Multiplexer #(.width(3), .enable("false")) multiplexer_6 (
    .in0(multiplexer_4_out), .in1(3'b010), .out(multiplexer_6_out), .sel(SBtype));
  Multiplexer #(.width(4), .enable("false")) multiplexer_7 (
    .in0(multiplexer_5_out), .in1(4'b0101), .out(multiplexer_7_out), .sel(mul));
  Multiplexer #(.width(2), .enable("false")) multiplexer_8 (
    .in0(2'b00), .in1(2'b01), .out(multiplexer_8_out), .sel(alu));
  Multiplexer #(.width(4), .enable("false")) multiplexer_9 (
    .in0(multiplexer_7_out), .in1(4'b0110), .out(multiplexer_9_out), .sel(mulhu));
  Multiplexer #(.width(3), .enable("false")) multiplexer_10 (
    .in0(multiplexer_6_out), .in1(3'b011), .out(multiplexer_10_out), .sel(Utype));
  Multiplexer #(.width(2), .enable("false")) multiplexer_11 (
    .in0(multiplexer_8_out), .in1(2'b10), .out(d_src), .sel(or_11_out));
  or or_11 (or_11_out, Itype_jalr, UJtype);
  Comparator #(.width(3)) comparator_53 (.a(inst[14:12]), .b(3'b000), .eq(comparator_53_eq));  // open: gt, lt
  Comparator #(.width(3)) comparator_54 (.a(inst[14:12]), .b(3'b100), .eq(comparator_54_eq));  // open: gt, lt
  Comparator #(.width(3)) comparator_55 (.a(inst[14:12]), .b(3'b110), .eq(comparator_55_eq));  // open: gt, lt
  Comparator #(.width(3)) comparator_56 (.a(inst[14:12]), .b(3'b001), .eq(comparator_56_eq));  // open: gt, lt
  Comparator #(.width(3)) comparator_57 (.a(inst[14:12]), .b(3'b111), .eq(comparator_57_eq));  // open: gt, lt
  or or_12 (or_12_out, bltu, bgeu);
  Multiplexer #(.width(4), .enable("false")) multiplexer_12 (
    .in0(multiplexer_9_out), .in1(4'b0111), .out(multiplexer_12_out), .sel(mulh));
  Multiplexer #(.width(4), .enable("false")) multiplexer_13 (
    .in0(multiplexer_12_out), .in1(4'b1000), .out(multiplexer_13_out), .sel(divu));
  Multiplexer #(.width(3), .enable("false")) multiplexer_14 (
    .in0(multiplexer_10_out), .in1(3'b100), .out(imm_sel), .sel(UJtype));
  Multiplexer #(.width(4), .enable("false")) multiplexer_15 (
    .in0(multiplexer_13_out), .in1(4'b1001), .out(multiplexer_15_out), .sel(div));
  and and_28 (beq, comparator_53_eq, SBtype);
  and and_29 (blt, comparator_54_eq, SBtype);
  and and_30 (bltu, comparator_55_eq, SBtype);
  and and_31 (bne, comparator_56_eq, SBtype);
  and and_32 (bgeu, comparator_57_eq, SBtype);
  and and_33 (BrUn, or_12_out, SBtype);
  Multiplexer #(.width(4), .enable("false")) multiplexer_16 (
    .in0(multiplexer_15_out), .in1(4'b1010), .out(multiplexer_16_out), .sel(remu));
  not not_2 (not_2_out, BrEq);
  not not_3 (not_3_out, BrLt);
  Multiplexer #(.width(4), .enable("false")) multiplexer_17 (
    .in0(multiplexer_16_out), .in1(4'b1011), .out(multiplexer_17_out), .sel(srl_type));
  Multiplexer #(.width(3), .enable("false")) multiplexer_18 (
    .in0(3'b000), .in1(3'b001), .out(multiplexer_18_out), .sel(lh));
  and and_34 (bne_type, bne, not_2_out);
  and and_35 (beq_type, beq, BrEq);
  and and_36 (blt_type, blt, BrLt);
  and and_37 (bgeu_type, bgeu, not_3_out);
  and and_38 (bltu_type, bltu, BrLt);
  Multiplexer #(.width(4), .enable("false")) multiplexer_19 (
    .in0(multiplexer_17_out), .in1(4'b1100), .out(multiplexer_19_out), .sel(s_r_a));
  Multiplexer #(.width(3), .enable("false")) multiplexer_20 (
    .in0(multiplexer_18_out), .in1(3'b010), .out(multiplexer_20_out), .sel(lhu));
  Multiplexer #(.width(4), .enable("false")) multiplexer_21 (
    .in0(multiplexer_19_out), .in1(4'b1101), .out(multiplexer_21_out), .sel(slti));
  Multiplexer #(.width(3), .enable("false")) multiplexer_22 (
    .in0(multiplexer_20_out), .in1(3'b011), .out(multiplexer_22_out), .sel(lb));
  Multiplexer #(.width(4), .enable("false")) multiplexer_23 (
    .in0(multiplexer_21_out), .in1(4'b1110), .out(alu_ctrl), .sel(sll_type));
  Multiplexer #(.width(3), .enable("false")) multiplexer_24 (
    .in0(multiplexer_22_out), .in1(3'b100), .out(load_type), .sel(lbu));

  // Other names for the same wires on the sheet: opcode[6:0] = inst[6:0]; func3[2:0] = inst[14:12];
  //   func7[6:0] = inst[31:25]; sw = mem_rw; Utype_lui = lui
endmodule

module CompLogic (
  input  [31:0] x_rs1,
  input  [31:0] x_rs2,
  input  BrUn,
  output BrLt,
  output BrEq
);

  wire comparator_1_eq, comparator_1_lt, comparator_2_eq, comparator_2_lt, not_1_out;

  Comparator #(.width(32)) comparator_1 (.a(x_rs1), .b(x_rs2), .eq(comparator_1_eq), .lt(comparator_1_lt));  // open: gt
  Comparator #(.width(32), .mode("unsigned")) comparator_2 (
    .a(x_rs1), .b(x_rs2), .eq(comparator_2_eq), .lt(comparator_2_lt));  // open: gt
  assign BrEq = not_1_out ? comparator_1_eq : 1'bz;  // Controlled_Buffer controlled_buffer_1
  assign BrLt = not_1_out ? comparator_1_lt : 1'bz;  // Controlled_Buffer controlled_buffer_2
  assign BrEq = BrUn ? comparator_2_eq : 1'bz;  // Controlled_Buffer controlled_buffer_3
  assign BrLt = BrUn ? comparator_2_lt : 1'bz;  // Controlled_Buffer controlled_buffer_4
  not not_1 (not_1_out, BrUn);

  // Other names for the same wires on the sheet: Br_Un = BrUn; out_eq = BrEq; out_lt = BrLt
endmodule

module Imm_Gen (
  input  [31:0] imm,
  input  [2:0] imm_sel,
  output [31:0] IMME
);

  wire [31:0] bit_extender_1_out, bit_extender_2_out, bit_extender_3_out, bit_extender_4_out;

  assign bit_extender_1_out = {{20{imm[31]}}, imm[31:20]};  // Bit_Extender bit_extender_1
  assign bit_extender_2_out = {{20{imm[31]}}, {imm[31:25], imm[11:7]}};  // Bit_Extender bit_extender_2
  assign bit_extender_3_out = {{19{imm[31]}}, {imm[31], imm[7], imm[30:25], imm[11:8], 1'b0}};  // Bit_Extender bit_extender_3
  assign bit_extender_4_out = {{19{imm[31]}}, {imm[31], imm[20], imm[30:21], 1'b0}};  // Bit_Extender bit_extender_4
  Multiplexer #(.select(3), .width(32), .enable("false")) multiplexer_1 (
    .in0(bit_extender_1_out), .in1(bit_extender_2_out), .in2(bit_extender_3_out),
    .in3({imm[31:12], {12{1'b0}}}), .in4(bit_extender_4_out), .out(IMME), .sel(imm_sel));  // open: in5, in6, in7
endmodule

module Data_Mem (
  input  [31:0] alu_res,
  input  mem_rw,
  input  clk,
  input  [31:0] x_rs2,
  input  [2:0] load_type,
  output [31:0] result
);

  wire comparator_1_eq, comparator_2_eq, comparator_3_eq, comparator_4_eq;
  wire [31:0] bit_extender_1_out, bit_extender_2_out, bit_extender_3_out, bit_extender_4_out,
       main_1_readdata, multiplexer_1_out, multiplexer_2_out, multiplexer_3_out;

  mem_main main_1 (.WriteAddr(alu_res), .WriteData(x_rs2), .MemRW(mem_rw), .ReadData(main_1_readdata), .clk(clk));
  Comparator #(.width(3)) comparator_1 (.a(load_type), .b(3'b001), .eq(comparator_1_eq));  // open: gt, lt
  Comparator #(.width(3)) comparator_2 (.a(load_type), .b(3'b000), .eq(comparator_2_eq));  // open: gt, lt
  Comparator #(.width(3)) comparator_3 (.a(load_type), .b(3'b100), .eq(comparator_3_eq));  // open: gt, lt
  Comparator #(.width(3)) comparator_4 (.a(load_type), .b(3'b010), .eq(comparator_4_eq));  // open: gt, lt
  assign bit_extender_1_out = {{24{1'b0}}, main_1_readdata[7:0]};  // Bit_Extender bit_extender_1
  assign bit_extender_2_out = {{24{main_1_readdata[7]}}, main_1_readdata[7:0]};  // Bit_Extender bit_extender_2
  assign bit_extender_3_out = {{16{main_1_readdata[15]}}, main_1_readdata[15:0]};  // Bit_Extender bit_extender_3
  assign bit_extender_4_out = {{16{1'b0}}, main_1_readdata[15:0]};  // Bit_Extender bit_extender_4
  Multiplexer #(.width(32), .enable("false")) multiplexer_1 (
    .in0(bit_extender_2_out), .in1(bit_extender_3_out), .out(multiplexer_1_out), .sel(comparator_1_eq));
  Multiplexer #(.width(32), .enable("false")) multiplexer_2 (
    .in0(multiplexer_1_out), .in1(main_1_readdata), .out(multiplexer_2_out), .sel(comparator_2_eq));
  Multiplexer #(.width(32), .enable("false")) multiplexer_3 (
    .in0(multiplexer_2_out), .in1(bit_extender_1_out), .out(multiplexer_3_out), .sel(comparator_3_eq));
  Multiplexer #(.width(32), .enable("false")) multiplexer_4 (
    .in0(multiplexer_3_out), .in1(bit_extender_4_out), .out(result), .sel(comparator_4_eq));

  // Other names for the same wires on the sheet: WriteAddr[31:0] = alu_res
endmodule
